// Logisim project nand2tetris.circ as structural Verilog
module my_or (
  input  ain,
  input  bin,
  output myout
);

  wire nand_1_out, nand_2_out;

  nand nand_1 (nand_1_out, ain, ain);
  nand nand_2 (nand_2_out, bin, bin);
  nand nand_3 (myout, nand_1_out, nand_2_out);
endmodule

module my_not (
  input  myin,
  output myout
);

  nand nand_1 (myout, myin, myin);
endmodule

module my_and (
  input  a,
  input  b,
  output MyOut
);

  wire nand_1_out, nand_2_out;

  nand nand_1 (nand_1_out, a, b);
  nand nand_2 (nand_2_out, a, b);
  nand nand_3 (MyOut, nand_1_out, nand_2_out);
endmodule

module my_XOR (
  input  a,
  input  b,
  output MyOut
);

  wire and_1_out, and_2_out, not_1_out, not_2_out;

  not not_1 (not_1_out, a);
  not not_2 (not_2_out, b);
  and and_1 (and_1_out, not_1_out, b);
  and and_2 (and_2_out, a, not_2_out);
  or or_1 (MyOut, and_1_out, and_2_out);
endmodule

module Mux (
  input  a,
  input  b,
  input  sel,
  output MyOut
);

  wire and_1_out, and_2_out, and_3_out, not_1_out, or_1_out;

  and and_1 (and_1_out, a, b);
  and and_2 (and_2_out, b, sel);
  and and_3 (and_3_out, a, not_1_out);
  not not_1 (not_1_out, sel);
  or or_1 (or_1_out, and_1_out, and_2_out);
  or or_2 (MyOut, or_1_out, and_3_out);
endmodule

module DMux (
  input  MyIn,
  input  sel,
  output a,
  output b
);

  wire not_1_out;

  not not_1 (not_1_out, sel);
  and and_1 (a, MyIn, not_1_out);
  and and_2 (b, MyIn, sel);
endmodule

module Not16 (
  input  [15:0] MyIn,
  output [15:0] MyOut
);

  assign MyOut = ~MyIn;  // NOT_Gate not_1, 16 bits wide
endmodule

module my_HA (
  input  a,
  input  b,
  output sum,
  output carry
);

  xor xor_1 (sum, a, b);
  and and_1 (carry, a, b);
endmodule

module my_FA (
  input  a,
  input  b,
  input  c,
  output sum,
  output carry
);

  wire and_1_out, and_2_out, and_3_out, and_4_out, xor_1_out;

  ExactlyOne xor_1 (.out(xor_1_out), .in0(a), .in1(b), .in2(c));
  and and_1 (and_1_out, a, b, c);
  and and_2 (and_2_out, b, c);
  and and_3 (and_3_out, c, a);
  and and_4 (and_4_out, a, b);
  or or_1 (carry, and_2_out, and_3_out, and_4_out);
  or or_2 (sum, xor_1_out, and_1_out);
endmodule

module my_FA2 (
  input  a,
  input  b,
  input  c,
  output sum,
  output carry
);

  wire my_ha_1_carry, my_ha_1_sum, my_ha_2_carry;

  my_HA my_ha_1 (.a(a), .b(b), .sum(my_ha_1_sum), .carry(my_ha_1_carry));
  my_HA my_ha_2 (.a(my_ha_1_sum), .b(c), .sum(sum), .carry(my_ha_2_carry));
  or or_1 (carry, my_ha_2_carry, my_ha_1_carry);
endmodule
